// Logisim project FINAL_COM_FOR.circ as structural Verilog
module main (
  input  [3:0] in_1,
  input  [3:0] in_2,
  input  [2:0] in_3,
  output [3:0] out_4
);

  ALU alu_1 (.A(in_1), .B(in_2), .opcode(in_3), .result(out_4));
endmodule

// VHDL entity ALU, as the project stores it:
library IEEE;
use IEEE.STD_LOGIC_1164.ALL;
use IEEE.NUMERIC_STD.ALL;

entity ALU is
    Port (
        A, B: in std_logic_vector(3 downto 0); -- Operandos de 4 bits
        opcode: in std_logic_vector(2 downto 0); -- Código de operação de 3 bits
        result: out std_logic_vector(3 downto 0) -- Resultado de 4 bits
        );
end ALU;

architecture Behavioral of ALU is
begin
    process(A, B, Opcode)
    begin
        case Opcode is
            when "000" => -- Soma
                Result <= std_logic_vector(unsigned(A) + unsigned(B));
            when "001" => -- Subtração
                Result <= std_logic_vector(unsigned(A) - unsigned(B));
            when "010" => -- AND
                Result <= A and B;
            when "011" => -- OR
                Result <= A or B;
            when "100" => -- NOT
                Result <= not A;
            when "101" => -- Deslocamento à esquerda
    			for i in 0 to 2 loop
        			Result(i) <= A(i+1);
    			end loop;
    			Result(3) <= '0';
		  when "110" => -- Deslocamento à direita
    			for i in 1 to 3 loop
        			Result(i) <= A(i-1);
    			end loop;
    			Result(0) <= '0';

            when others =>
                Result <= (others => '0');
        end case;
    end process;
end Behavioral;
