// Logisim project TRABALHOFINAL.circ as structural Verilog
module main (
  input  [3:0] in_1,
  input  [3:0] in_2,
  input  [2:0] in_3,
  output [3:0] out_4
);

  ULA_Testbench AA ();  // open: A, B, opcode, result
  ULA OOOO (.A(in_1), .B(in_2), .opcode(in_3), .result(out_4));
endmodule

// VHDL entity ULA, as the project stores it:
library IEEE;
use IEEE.STD_LOGIC_1164.ALL;
use IEEE.NUMERIC_STD.ALL;

entity ULA is
    Port (
        A, B: in std_logic_vector(3 downto 0); -- Operandos de 4 bits
        opcode: in std_logic_vector(2 downto 0); -- Código de operação de 3 bits
        result: out std_logic_vector(3 downto 0) -- Resultado de 4 bits
    );
end ULA;

architecture Behavioral of ULA is
begin

    process(A, B, opcode)
    begin
        case opcode is
            when "000" => -- Soma
                result <= std_logic_vector(unsigned(A) + unsigned(B));
            when "001" => -- Subtração
                result <= std_logic_vector(unsigned(A) - unsigned(B));
            when "010" => -- AND
                result <= A and B;
            when "011" => -- OR
                result <= A or B;
            when "100" => -- NOT
                result <= not A;
            when "101" => -- Deslocamento à esquerda
                result <= A(2 downto 0) & '0';
            when "110" => -- Deslocamento à direita
                result <= '0' & A(3 downto 1);
            when others =>
                result <= (others => 'X'); -- Código de operação inválido
        end case;
    end process;

end Behavioral;

// VHDL entity ULA_Testbench, as the project stores it:
library IEEE;
use IEEE.STD_LOGIC_1164.ALL;

entity ULA_Testbench is
end ULA_Testbench;

architecture Behavioral of ULA_Testbench is

    component ULA
        Port (
            A, B: in std_logic_vector(3 downto 0);
            opcode: in std_logic_vector(2 downto 0);
            result: out std_logic_vector(3 downto 0)
        );
    end component;

    signal A, B, opcode: std_logic_vector(3 downto 0);
    signal result: std_logic_vector(3 downto 0);

begin

    ULA_inst: ULA port map (A, B, opcode, result);

    stimulus_process: process
    begin
        A <= "0000"; B <= "0000"; opcode <= "000"; -- Soma (0 + 0)
        wait for 10 ns;
        
        A <= "0001"; B <= "0010"; opcode <= "001"; -- Subtração (1 - 2)
        wait for 10 ns;
        
        -- Adicione mais casos de teste conforme necessário
        
        wait;
    end process stimulus_process;

end Behavioral;
